# Fritzing sketch beacon_diagram (saved by Fritzing 0.9.4)
breadboards: 1

parts:
  Argon1 = Particle Argon
  GY1 = MPU-6050 Board GY-521 [form="♀ (female)" package=THT]
  M1 = BMP280
  U1 = GPS6MV2 [package=GSP6MV2]
  LED1 = smd LED [color="White (6500K)" package="1206 [SMD]"]
  LED2 = smd LED [color="White (6500K)" package="1206 [SMD]"]
  ESP32_-_Back1 = ESP32 - CAM
  BAT1 = Battery Holders [package=lipo-1100mAh]  # not connected

nets:
  3.3V: Argon1.3.3V, GY1.pin1, M1.VIN, U1.VCC
  GND: Argon1.GND, GY1.pin2, M1.GND, U1.GND, LED1.anode, LED2.anode, ESP32_-_Back1.GND
  N1: Argon1.MI, LED1.cathode, LED2.cathode
  N2: Argon1.RX, U1.TX-O
  N3: Argon1.TX, U1.RX-I
  N4: Argon1.SDA, GY1.pin4
  N5: Argon1.SCL, GY1.pin3
  N6: Argon1.LI+, ESP32_-_Back1.3.3V

custom parts:
  Particle Argon: The Argon is a powerful Wi-Fi enabled development board that can act as either a standalone Wi-Fi endpoint or Wi-Fi enabled gateway for Particle Mesh networks. It is based on the Nordic nRF52840 and has built-in battery charging circuitry so it’s easy to connect a Li-Po and deploy your local network in minutes. The Argon is great for connecting existing projects to the Particle Device Cloud or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
  MPU-6050 Board GY-521: Acelerometro y Giroscopio MPU-6050 Board GY-521
  BMP280: Temperature Humidity Barometric presure Sensor, I2C
  GPS6MV2: GPS transciever
  ESP32 - CAM: The ESP32-CAM has a very competitive small-size camera module that can operate independently as a minimum system with a footprint of only 27*40.5*4.5mm and a deep sleep current of up to 6mA.
