# Fritzing sketch payload_release_diagram (saved by Fritzing 0.9.4)
breadboards: 1

parts:
  Teensy_3_1 = Teensy 3.1
  J1 = Basic Servo
  S1 = Pushbutton [package="[THT]"]

nets:
  GND: Teensy_3_1.GND, J1.gnd
  N1: Teensy_3_1.D2, S1.Pin_1, S1.Pin_2
  N2: Teensy_3_1.A6/D20, J1.pulse
  3V3: Teensy_3_1.3V3, J1.vcc, S1.Pin_3, S1.Pin_4

custom parts:
  Pushbutton: A generic pushbutton.
